// Logisim project lab2 (5).circ as structural Verilog: 1 circuit, main circuit main
module main (
  output [3:0] out_1,
  output [3:0] out_2,
  output [3:0] out_3,
  output [3:0] out_4,
  output [3:0] out_5
);

  wire and_1_out, and_2_out, and_3_out, and_4_out, and_5_out, and_6_out, and_7_out, and_8_out, and_9_out,
       and_10_out, and_11_out, and_15_out, and_16_out, and_17_out, and_18_out, and_19_out, and_20_out,
       and_21_out, and_22_out, and_23_out, and_24_out, and_25_out, and_26_out, and_27_out, and_28_out,
       and_29_out, and_30_out, and_31_out, and_32_out, and_33_out, and_34_out, and_35_out, and_41_out,
       and_42_out, and_44_out, and_45_out, and_46_out, and_47_out, and_49_out, and_50_out, and_51_out,
       and_52_out, and_53_out, and_54_out, and_55_out, and_56_out, and_57_out, and_58_out, and_59_out, clear,
       clk, comparator_1_eq, comparator_2_eq, comparator_3_eq, comparator_4_eq, comparator_5_eq,
       comparator_6_eq, comparator_7_eq, comparator_8_eq, comparator_9_lt, comparator_10_eq,
       comparator_11_eq, comparator_11_lt, comparator_12_eq, controlled_buffer_2_out,
       controlled_buffer_6_out, controlled_buffer_10_out, controlled_buffer_14_out, counter_1_carry,
       counter_2_carry, counter_3_carry, counter_4_carry, counter_5_carry, counter_6_carry, counter_7_carry,
       counter_8_carry, counter_9_carry, counter_11_carry, h_clear, i1, i2, i3, i4, i5, i7, i8, L1, L2, L4,
       L5, L6, L7, L8, m, not_7_out, not_8_out, not_9_out, not_10_out, not_11_out, not_12_out, not_13_out,
       not_14_out, Nq1, Nq2, Nq3, Nq4, Nx1, Nx2, or_13_out, or_14_out, or_15_out, or_16_out, or_17_out,
       or_18_out, or_19_out, or_20_out, or_21_out, or_22_out, p, press, s, s_r_ff_1_q, sig, sm, x1, x2;
  wire [2:0] counter_2_q, counter_5_q, counter_6_q, counter_8_q, counter_10_q;
  wire [3:0] bit_extender_2_out, bit_extender_3_out, bit_extender_4_out, bit_extender_5_out,
       controlled_buffer_15_out, counter_3_q, counter_7_q, counter_11_q, h_dec, h_ed, h_ed2, m_ed2, min_dec,
       min_dec_t, min_ed, min_ed_t, multiplexer_1_out, multiplexer_2_out, multiplier_1_out, multiplier_2_out,
       sec_c, sec_dec, sec_ed, week;

  not not_1 (Nx1, x1);
  not not_2 (Nx2, x2);
  not not_3 (Nq1, out_4[3]);
  not not_4 (Nq2, out_4[2]);
  not not_5 (Nq3, out_4[1]);
  not not_6 (Nq4, out_4[0]);
  and and_1 (and_1_out, x2, Nq3, out_4[0]);
  and and_2 (and_2_out, x2, Nq2, out_4[0]);
  and and_3 (and_3_out, Nx1, Nx2, out_4[3]);
  and and_4 (and_4_out, Nx1, Nq3, out_4[0]);
  and and_5 (and_5_out, Nx1, Nq2, out_4[0]);
  and and_6 (and_6_out, x1, Nx2, Nq2, out_4[1], Nq4);
  and and_7 (and_7_out, x1, Nx2, Nq1, Nq3, Nq4);
  and and_8 (and_8_out, Nx1, x2, Nq1, Nq2, Nq3);
  and and_9 (and_9_out, Nq1, out_4[2], Nq3);
  and and_10 (and_10_out, Nq1, out_4[1], Nq4);
  and and_11 (and_11_out, Nq1, Nq2, out_4[0]);
  and and_12 (L2, Nq1, out_4[2], out_4[0], out_4[1]);
  and and_13 (L4, out_4[3], Nq2, Nq3);
  and and_14 (L5, out_4[0], out_4[3], Nq2, Nq3);
  and and_15 (and_15_out, Nq1, Nq2, Nq3, Nq4);
  and and_16 (and_16_out, Nq1, out_4[2], Nq3, out_4[0]);
  and and_17 (and_17_out, Nq1, out_4[2], out_4[1], Nq4);
  and and_18 (and_18_out, Nq1, out_4[1], Nq4);
  and and_19 (and_19_out, Nq2, Nq3);
  and and_20 (and_20_out, Nq1, Nq3, Nq4);
  and and_21 (and_21_out, Nq1, out_4[2], Nq4);
  and and_22 (and_22_out, Nq1, Nq2, out_4[1], out_4[0]);
  and and_23 (and_23_out, x2, out_4[3]);
  and and_24 (and_24_out, out_4[3], out_4[0]);
  and and_25 (and_25_out, Nx1, Nx2, Nq2, Nq3, Nq4);
  and and_26 (and_26_out, x2, out_4[2], Nq3);
  and and_27 (and_27_out, Nq3, out_4[2], Nq4);
  and and_28 (and_28_out, Nx1, out_4[2], Nq3);
  and and_29 (and_29_out, x2, Nq1, Nq3, Nq4);
  and and_30 (and_30_out, x1, Nx2, out_4[1], Nq2, out_4[0]);
  and and_31 (and_31_out, x2, Nq2, out_4[1]);
  and and_32 (and_32_out, Nq2, out_4[1], Nq4);
  and and_33 (and_33_out, Nx1, Nq2, out_4[1]);
  and and_34 (and_34_out, x2, Nq1, Nq2, Nq4);
  and and_35 (and_35_out, x1, Nx2, Nq1, Nq2, Nq3, out_4[0]);
  or or_1 (L7, and_18_out, and_19_out);
  or or_2 (out_3[0], and_1_out, and_2_out, and_3_out, and_4_out, and_5_out, and_6_out, and_7_out, and_8_out);
  or or_3 (L1, and_9_out, and_10_out, and_11_out);
  or or_4 (L6, and_15_out, and_16_out, and_17_out);
  or or_5 (L8, and_20_out, and_21_out, and_22_out);
  or or_6 (out_3[3], and_23_out, and_24_out, and_25_out);
  or or_7 (out_3[2], and_26_out, and_27_out, and_28_out, and_29_out, and_30_out);
  or or_8 (out_3[1], and_31_out, and_32_out, and_33_out, and_34_out, and_35_out);
  Register #(.trigger("falling"), .width(4)) register_1 (.D(out_3), .clk(press), .Q(out_4));  // open: en, clr
  Button u_S (.out(s));
  and and_36 (i1, Nx1, Nx2, Nq1, Nq2, Nq3, out_4[0]);
  and and_37 (i2, Nx1, Nx2, Nq1, Nq2, out_4[1], Nq4);
  and and_38 (i3, Nx1, Nx2, Nq1, Nq2, out_4[1], out_4[0]);
  and and_39 (i4, Nx1, Nx2, Nq1, out_4[2], Nq3, Nq4);
  and and_40 (i5, Nx1, Nx2, Nq1, out_4[2], Nq3, out_4[0]);
  and and_41 (and_41_out, x1, Nx2, out_4[3], Nq2, Nq3, out_4[0]);
  and and_42 (and_42_out, x1, x2, out_4[3], Nq2, Nq3, Nq4);
  and and_43 (i8, Nx1, x2, out_4[3], Nq2, Nq3, Nq4);
  Button u_M (.out(m));
  or or_9 (press, s, m, p, sm);
  or or_10 (x1, m, sm);
  Hex_Digit_Display hex_digit_display_1 (.value(week));  // open: dp
  Button u_P (.out(p));
  Button u_SM (.out(sm));
  or or_11 (x2, p, sm);
  Hex_Digit_Display hex_digit_display_2 (.value(h_dec));  // open: dp
  or or_12 (i7, and_41_out, and_42_out);
  Hex_Digit_Display hex_digit_display_3 (.value(h_ed));  // open: dp
  Hex_Digit_Display hex_digit_display_4 (.value(multiplexer_1_out));  // open: dp
  Multiplexer #(.width(4)) multiplexer_1 (.in0(min_dec), .in1(min_dec_t), .out(multiplexer_1_out), .sel(L4));
  Hex_Digit_Display hex_digit_display_5 (.value(multiplexer_2_out), .dp(multiplexer_2_out[0]));
  Multiplexer #(.width(4)) multiplexer_2 (.in0(min_ed), .in1(min_ed_t), .out(multiplexer_2_out), .sel(L4));
  Comparator #(.width(4)) comparator_1 (.a(min_ed), .b(4'b0000), .eq(comparator_1_eq));  // open: gt, lt
  Comparator #(.width(4)) comparator_2 (.a(min_dec), .b(4'b0000), .eq(comparator_2_eq));  // open: gt, lt
  Comparator #(.width(4)) comparator_3 (.a(min_ed), .b(4'b0101), .eq(comparator_3_eq));  // open: gt, lt
  Comparator #(.width(4)) comparator_4 (.a(min_dec), .b(4'b0001), .eq(comparator_4_eq));  // open: gt, lt
  Comparator #(.width(4)) comparator_5 (.a(min_ed), .b(4'b0000), .eq(comparator_5_eq));  // open: gt, lt
  Comparator #(.width(4)) comparator_6 (.a(min_dec), .b(4'b0011), .eq(comparator_6_eq));  // open: gt, lt
  Comparator #(.width(4)) comparator_7 (.a(min_ed), .b(4'b0101), .eq(comparator_7_eq));  // open: gt, lt
  Comparator #(.width(4)) comparator_8 (.a(min_dec), .b(4'b0100), .eq(comparator_8_eq));  // open: gt, lt
  Hex_Digit_Display hex_digit_display_6 (.value(sec_dec));  // open: dp
  Hex_Digit_Display hex_digit_display_7 (.value(sec_ed));  // open: dp
  and and_44 (and_44_out, comparator_1_eq, comparator_2_eq);
  and and_45 (and_45_out, comparator_3_eq, comparator_4_eq);
  and and_46 (and_46_out, comparator_5_eq, comparator_6_eq);
  and and_47 (and_47_out, comparator_7_eq, comparator_8_eq);
  LED led_1 (.in(sig));
  or or_13 (or_13_out, and_44_out, and_45_out, and_46_out, and_47_out);
  Comparator #(.mode("unsigned"), .width(4)) comparator_9 (
    .a(out_1), .b(4'b0100), .lt(comparator_9_lt));  // open: gt, eq
  Comparator #(.mode("unsigned"), .width(4)) comparator_10 (
    .a(out_2), .b(4'b0000), .eq(comparator_10_eq));  // open: gt, lt
  Clock clock_1 (.out(clk));
  and and_48 (sig, comparator_9_lt, comparator_10_eq, or_13_out);
  not not_7 (not_7_out, L1);
  Counter #(.max('h9), .trigger("falling"), .width(4)) counter_1 (
    .clk(and_49_out), .carry(counter_1_carry), .Q(out_1));  // open: clr, load, up, count, D
  and and_49 (and_49_out, clk, not_7_out);
  and and_50 (and_50_out, L4, s);
  and and_51 (and_51_out, L5, sm);
  Counter #(.max('h6), .trigger("falling"), .width(3)) counter_2 (
    .clr(counter_2_carry), .clk(counter_1_carry), .carry(counter_2_carry), .Q(counter_2_q));  // open: load, up, count, D
  S_R_Flip_Flop #(.trigger("falling")) s_r_ff_1 (
    .S(or_14_out), .Q(s_r_ff_1_q), .reset(i7), .preset(or_14_out));  // open: R, clk, Qn
  or or_14 (or_14_out, and_50_out, and_51_out);
  assign out_2 = {{1{1'b0}}, counter_2_q};  // Bit_Extender bit_extender_1
  Counter #(.max('h9), .trigger("falling"), .width(4)) counter_3 (
    .clr(i8), .clk(and_52_out), .carry(counter_3_carry), .Q(counter_3_q));  // open: load, up, count, D
  and and_52 (and_52_out, s_r_ff_1_q, clk);
  Multiplier #(.width(4)) multiplier_1 (.a(out_2), .b(4'b1010), .out(multiplier_1_out));  // open: cin, cout
  and and_53 (and_53_out, s, i1);
  Adder #(.width(4)) adder_1 (.a(multiplier_1_out), .b(out_1), .out(sec_c));  // open: cin, cout
  Counter #(.max('ha), .trigger("falling"), .width(4)) counter_4 (
    .clr(counter_4_carry), .clk(or_15_out), .carry(counter_4_carry), .Q(m_ed2));  // open: load, up, count, D
  or or_15 (or_15_out, and_53_out, counter_2_carry);
  assign sec_ed = L4 ? counter_3_q : 4'bz;  // Controlled_Buffer controlled_buffer_1
  Counter #(.max('h5), .trigger("falling"), .width(3)) counter_5 (
    .clr(i8), .clk(counter_3_carry), .carry(counter_5_carry), .Q(counter_5_q));  // open: load, up, count, D
  not not_8 (not_8_out, i1);
  assign controlled_buffer_2_out = not_8_out ? counter_4_carry : 1'bz;  // Controlled_Buffer controlled_buffer_2
  and and_54 (and_54_out, L7, not_9_out);
  assign min_ed = and_54_out ? m_ed2 : 4'bz;  // Controlled_Buffer controlled_buffer_3
  and and_55 (and_55_out, s, i2);
  not not_9 (not_9_out, L4);
  assign bit_extender_2_out = {{1{1'b0}}, counter_5_q};  // Bit_Extender bit_extender_2
  assign sec_dec = L4 ? bit_extender_2_out : 4'bz;  // Controlled_Buffer controlled_buffer_4
  Counter #(.max('h6), .trigger("falling"), .width(3)) counter_6 (
    .clr(counter_6_carry), .clk(or_16_out), .carry(counter_6_carry), .Q(counter_6_q));  // open: load, up, count, D
  or or_16 (or_16_out, and_55_out, controlled_buffer_2_out);
  Counter #(.max('h9), .trigger("falling"), .width(4)) counter_7 (
    .clr(or_18_out), .clk(counter_5_carry), .carry(counter_7_carry), .Q(counter_7_q));  // open: load, up, count, D
  assign bit_extender_3_out = {{1{1'b0}}, counter_6_q};  // Bit_Extender bit_extender_3
  assign min_ed_t = L4 ? counter_7_q : 4'bz;  // Controlled_Buffer controlled_buffer_5
  not not_10 (not_10_out, i2);
  assign controlled_buffer_6_out = not_10_out ? counter_6_carry : 1'bz;  // Controlled_Buffer controlled_buffer_6
  assign min_dec = L7 ? bit_extender_3_out : 4'bz;  // Controlled_Buffer controlled_buffer_7
  Counter #(.max('h6), .trigger("falling"), .width(3)) counter_8 (
    .clr(or_18_out), .clk(counter_7_carry), .carry(counter_8_carry), .Q(counter_8_q));  // open: load, up, count, D
  or or_17 (or_17_out, clear, counter_9_carry);
  and and_56 (and_56_out, s, i3);
  Multiplier #(.width(4)) multiplier_2 (.a(min_dec), .b(4'b1010), .out(multiplier_2_out));  // open: cin, cout
  or or_18 (or_18_out, i8, counter_8_carry);
  Counter #(.max('ha), .trigger("falling"), .width(4)) counter_9 (
    .clr(or_17_out), .clk(or_19_out), .carry(counter_9_carry), .Q(h_ed2));  // open: load, up, count, D
  or or_19 (or_19_out, controlled_buffer_6_out, and_56_out);
  Adder #(.width(4)) adder_2 (.a(m_ed2), .b(multiplier_2_out), .out(out_5));  // open: cin, cout
  assign bit_extender_4_out = {{1{1'b0}}, counter_8_q};  // Bit_Extender bit_extender_4
  assign h_ed = L8 ? h_ed2 : 4'bz;  // Controlled_Buffer controlled_buffer_8
  assign min_dec_t = L4 ? bit_extender_4_out : 4'bz;  // Controlled_Buffer controlled_buffer_9
  not not_11 (not_11_out, i3);
  assign controlled_buffer_10_out = not_11_out ? counter_9_carry : 1'bz;  // Controlled_Buffer controlled_buffer_10
  Counter #(.max('h2), .trigger("falling"), .width(3)) counter_10 (
    .clr(h_clear), .clk(or_20_out), .Q(counter_10_q));  // open: load, up, count, D, carry
  or or_20 (or_20_out, controlled_buffer_10_out, and_57_out);
  and and_57 (and_57_out, s, i4);
  assign bit_extender_5_out = {{1{1'b0}}, counter_10_q};  // Bit_Extender bit_extender_5
  assign h_dec = L8 ? bit_extender_5_out : 4'bz;  // Controlled_Buffer controlled_buffer_11
  Comparator #(.mode("unsigned"), .width(4)) comparator_11 (
    .a(4'b0100), .b(h_ed2), .eq(comparator_11_eq), .lt(comparator_11_lt));  // open: gt
  Comparator #(.mode("unsigned"), .width(4)) comparator_12 (
    .a(4'b0010), .b(bit_extender_5_out), .eq(comparator_12_eq));  // open: gt, lt
  or or_21 (or_21_out, comparator_11_eq, comparator_11_lt);
  not not_12 (not_12_out, i4);
  and and_58 (and_58_out, or_21_out, comparator_12_eq);
  assign clear = not_12_out ? and_58_out : 1'bz;  // Controlled_Buffer controlled_buffer_12
  not not_13 (not_13_out, i3);
  assign h_clear = not_13_out ? and_58_out : 1'bz;  // Controlled_Buffer controlled_buffer_13
  and and_59 (and_59_out, s, i5);
  Counter #(.max('h7), .trigger("falling"), .width(4)) counter_11 (
    .clr(counter_11_carry), .clk(or_22_out), .carry(counter_11_carry), .Q(counter_11_q));  // open: load, up, count, D
  or or_22 (or_22_out, and_59_out, controlled_buffer_14_out);
  assign controlled_buffer_14_out = not_14_out ? clear : 1'bz;  // Controlled_Buffer controlled_buffer_14
  not not_14 (not_14_out, i3);
  assign controlled_buffer_15_out = L6 ? counter_11_q : 4'bz;  // Controlled_Buffer controlled_buffer_15
  Adder #(.width(4)) adder_3 (.a(controlled_buffer_15_out), .b(4'b0001), .out(week));  // open: cin, cout
  // Pins of 1 and 4 bits meet at multiplexer_2_out

  // Other names for the same wires on the sheet: min_c[3:0] = out_5; Q4 = out_3[0]; Q3 = out_3[1]; Q2 = out_3[2];
  //   Q1 = out_3[3]; q4_t = out_4[0]; q_4 = out_4[0]; q3_t = out_4[1]; q_3 = out_4[1]; q2_t = out_4[2];
  //   q_2 = out_4[2]; q1_t = out_4[3]; q_1 = out_4[3]; sec_dec_c[3:0] = out_2; seq_ed_c[3:0] = out_1

  // Notes on the sheet:
  //   L4
  //   Q4
  //   L1
  //   L2
  //   L5
  //   L6
  //   L7
  //   Q2
  //   L8
  //   Q1
  //   Q3
  //   i1
  //   i2
  //   i3
  //   i4
  //   i5
  //   i7
  //   i8
  //   <<звуковой сигнал>>
  //   секундомер
endmodule
